// Logisim project alu.circ as structural Verilog: 2 circuits, main circuit alu
module alu (
  input  [31:0] A,
  input  [31:0] B,
  input  [3:0] ALUSel,
  output [31:0] Result
);

  wire adder_5_cout, xor_2_out;
  wire [0:0] slt7;
  wire [31:0] A2s, add0, adder_1_out, adder_2_out, adder_3_out, and1, B2s, bit_extender_1_out, cal2s_1_out_2,
       cal2s_2_out_2, divu8, mul10, mulh14, mulhu11, multiplexer_2_out, multiplexer_3_out, multiplier_1_cout,
       multiplier_1_out, multiplier_2_out, not_1_out, not_2_out, not_3_out, not_4_out, or2, remu9, sll6,
       sra5, srl4, sub12, xor3;

  assign not_1_out = ~A;  // NOT_Gate not_1, 32 bits wide
  Adder #(.width(32)) adder_1 (.a(not_1_out), .b(32'h1), .out(adder_1_out));  // open: cin, cout
  Multiplexer #(.width(32), .enable("false")) multiplexer_1 (.in0(A), .in1(adder_1_out), .out(A2s), .sel(A[31]));
  Multiplexer #(.width(32), .enable("false")) multiplexer_2 (
    .in0(A), .in1(cal2s_1_out_2), .out(multiplexer_2_out), .sel(A[31]));
  cal2s cal2s_1 (.out_2(cal2s_1_out_2), .in_1(A));  // open: out_3
  Multiplexer #(.width(32), .enable("false")) multiplexer_3 (
    .in0(B), .in1(cal2s_2_out_2), .out(multiplexer_3_out), .sel(B[31]));
  cal2s cal2s_2 (.out_2(cal2s_2_out_2), .in_1(B));  // open: out_3
  assign not_2_out = ~B;  // NOT_Gate not_2, 32 bits wide
  Multiplier #(.width(32)) multiplier_1 (
    .a(multiplexer_2_out), .b(multiplexer_3_out), .out(multiplier_1_out), .cout(multiplier_1_cout));  // open: cin
  assign not_3_out = ~multiplier_1_cout;  // NOT_Gate not_3, 32 bits wide
  Comparator #(.width(32)) comparator_1 (.a(A), .b(B), .lt(slt7[0]));  // open: gt, eq
  Adder #(.width(32)) adder_2 (.a(not_2_out), .b(32'h1), .out(adder_2_out));  // open: cin, cout
  assign not_4_out = ~multiplier_1_out;  // NOT_Gate not_4, 32 bits wide
  Adder #(.width(32)) adder_3 (.a(bit_extender_1_out), .b(not_3_out), .out(adder_3_out));  // open: cin, cout
  Adder #(.width(32)) adder_4 (.a(A), .b(B), .out(add0));  // open: cin, cout
  assign and1 = A & B;  // AND_Gate and_1, 32 bits wide
  assign or2 = A | B;  // OR_Gate or_1, 32 bits wide
  assign xor3 = A ^ B;  // XOR_Gate xor_1, 32 bits wide
  Shifter #(.width(32), .shift("lr")) shifter_1 (.in(A), .\dist (B[4:0]), .out(srl4));
  Shifter #(.width(32), .shift("ar")) shifter_2 (.in(A), .\dist (B[4:0]), .out(sra5));
  Shifter #(.width(32)) shifter_3 (.in(A), .\dist (B[4:0]), .out(sll6));
  Multiplexer #(.width(32), .enable("false")) multiplexer_4 (.in0(B), .in1(adder_2_out), .out(B2s), .sel(B[31]));
  Adder #(.width(32)) adder_5 (.a(32'h1), .b(not_4_out), .cout(adder_5_cout));  // open: out, cin
  Multiplexer #(.width(32), .enable("false")) multiplexer_5 (
    .in0(multiplier_1_cout), .in1(adder_3_out), .out(mulh14), .sel(xor_2_out));
  xor xor_2 (xor_2_out, A[31], B[31]);
  assign bit_extender_1_out = {{31{adder_5_cout}}, adder_5_cout};  // Bit_Extender bit_extender_1
  Multiplier #(.width(32)) multiplier_2 (.a(B), .b(divu8), .out(multiplier_2_out));  // open: cin, cout
  Divider #(.width(32)) divider_1 (.a(A), .b(B), .out(divu8));  // open: upper, rem
  Subtractor #(.width(32)) subtractor_1 (.a(A), .b(multiplier_2_out), .out(remu9));  // open: bin, bout
  Multiplier #(.width(32)) multiplier_3 (.a(A), .b(B), .out(mul10), .cout(mulhu11));  // open: cin
  Subtractor #(.width(32)) subtractor_2 (.a(A), .b(B), .out(sub12));  // open: bin, bout
  Multiplexer #(.select(4), .width(32), .enable("false")) multiplexer_6 (
    .in0(add0), .in1(and1), .in2(or2), .in3(xor3), .in4(srl4), .in5(sra5), .in6(sll6),
    .in7({{31{1'b0}}, slt7[0]}), .in8(divu8), .in9(remu9), .in10(mul10), .in11(mulhu11), .in12(sub12),
    .in13(B), .in14(mulh14), .out(Result), .sel(ALUSel));  // open: in15

  // Other names for the same wires on the sheet: bsel13[31:0] = B

  // Notes on the sheet:
  //   INPUTS to your circuit
  //   DON'T CHANGE THE LOCATIONS OF THE INPUTS AND OUTPUTS!
  //   OUTPUT from your circuit
endmodule

module cal2s (
  input  [31:0] in_1,
  output [31:0] out_2,
  output out_3
);

  wire [31:0] not_1_out;

  assign not_1_out = ~in_1;  // NOT_Gate not_1, 32 bits wide
  Adder #(.width(32)) adder_1 (.a(not_1_out), .b(32'h1), .out(out_2), .cout(out_3));  // open: cin
endmodule
